# Fritzing sketch DiffDrive-ESP32-WROVER-C1 (saved by Fritzing 0.9.6b)

parts:
  Part1 = Adafruit DRV8833 DC/Stepper Motor Driver [part_number="Adafruit #3297"]
  M18 = RioRand LM2596
  BAT1 = Battery Holders [package=lipo-1100mAh]
  BAT2 = Battery Holders [package=lipo-1100mAh]
  M19 = RPlidar A1M8 [package=THT]
  S1 = Toggle Switch [package=THT]
  U3 = Voltage Regulator [part_number=LM317 package=to220-adj]
  U4 = Voltage Regulator [part_number=LM317 package=to220-adj]
  R7 = Resistor [tolerance=±5% resistance=100 package="0603 [SMD]"]
  C3 = Ceramic Capacitor [capacitance=100nF voltage=35V package="100 mil [THT, multilayer]"]
  C4 = Ceramic Capacitor [capacitance=100nF voltage=35V package="100 mil [THT, multilayer]"]
  R8 = Trimmer Potentiometer [maximum_resistance=0pΩ part_number="1 kohm" package=THT]
  R9 = Resistor [tolerance=±5% resistance=680 package="0805 [SMD]"]
  R10 = Resistor [tolerance=±5% resistance=220 package="0603 [SMD]"]
  R11 = Resistor [tolerance=±5% resistance=1 package="0603 [SMD]"]
  C5 = Ceramic Capacitor [capacitance=100nF voltage=35V package="100 mil [THT, multilayer]"]
  Part2 = Adafruit INA219 [part_number="Adafruit #904"]
  Q1 = Basic FET P-Channel [part_number=IRF4905 package="DPak [SMD]"]
  D1 = Schottky Diode [part_number=1N5819 package="300 mil [THT]"]
  R12 = Resistor [tolerance=±5% resistance=100k package="0603 [SMD]"]
  DC_Mot_Enc1 = DC Motor with two-phase hall-encoder [part_number=VT-E-G25A-06-177E]
  DC_Mot_Enc2 = DC Motor with two-phase hall-encoder [part_number=VT-E-G25A-06-177E]
  A1 = ESP32 wrover cam

nets:
  N1: Part1.AOUT2, DC_Mot_Enc2.pin1
  N2: Part1.AOUT1, DC_Mot_Enc2.pin2
  N3: Part1.BOUT1, DC_Mot_Enc1.pin1
  N4: Part1.BOUT2, DC_Mot_Enc1.pin2
  N5: Part1.VMOTOR, Part1.!SLEEP, M18.Pin_3, M19.pin3, A1.Pin_19
  GND: Part1.GND, M18.Pin_4, M19.pin4, Part2.GND, DC_Mot_Enc1.pin4, DC_Mot_Enc2.pin4, A1.Pin_14, A1.Pin_40
  N6: Part1.BIN1, A1.Pin_11
  N7: Part1.BIN2, A1.Pin_7
  N8: Part1.AIN2, A1.Pin_13
  N9: Part1.AIN1, A1.Pin_28
  N10: M18.Pin_1, S1.L2
  N11: M18.Pin_2, BAT2.-, C3.0, C4.0, R8.leg2, C5.0, R12.Pin_1
  N12: BAT1.+, Part2.VIN+
  N13: BAT1.-, BAT2.+
  N14: M19.pin1, A1.Pin_39
  N15: S1.COM, Q1.source, D1.cathode
  N16: U3.ADJ, R9.Pin_1, R10.Pin_0
  N17: U3.IN, R10.Pin_1, C5.1, Part2.VIN-, Q1.drain
  N18: U3.OUT, R7.Pin_1, C3.1, R11.Pin_1
  N19: U4.ADJ, R7.Pin_0
  N20: U4.IN, R11.Pin_0
  N21: U4.OUT, C4.1, Q1.Gate, D1.anode, R12.Pin_0
  N22: R8.wiper, R9.Pin_0
  N23: Part2.VCC, DC_Mot_Enc1.pin3, DC_Mot_Enc2.pin3, A1.Pin_1
  N24: Part2.SCL, A1.Pin_38
  N25: Part2.SDA, A1.Pin_35
  N26: DC_Mot_Enc1.pin5, A1.Pin_10
  N27: DC_Mot_Enc1.pin6, A1.Pin_8
  N28: DC_Mot_Enc2.pin5, A1.Pin_12
  N29: DC_Mot_Enc2.pin6, A1.Pin_15

notes:
  12 V
  Wheel encoders inputs
  brown IO33 GREEN-WHITE
  white IO26 GREEN
  yellow IO14 ORANGE
  grey IO13 ORANGE-WHITE

custom parts:
  Adafruit DRV8833 DC/Stepper Motor Driver: Spin two DC motors or step one bi-polar or uni-polar stepper with up to 1.2A per channel using the DRV8833. This motor driver chip is a nice alternative to the TB6612 driver. Like that chip, you get 2 full H-bridges, but this chip is better for low voltage uses (can run from 2.7V up to 10.8V motor power) and has built in current limiting capability. We set it up for 1A current limiting so you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
  RPlidar A1M8: .The RPLIDAR A1 is the next generation low cost 360 degree 2D laser scanner (LIDAR) solution developed by SLAMTEC. It can take up to 4000 samples of laser ranging per second with high rotation speed. And equipped with SLAMTEC patented OPTMAG technology, it breakouts the life limitation of traditional LIDAR system so as to work stably for a long time.
  Adafruit INA219: This breakout board will solve all your power-monitoring problems. Instead of struggling with two multimeters, you can just use the handy INA219B chip on this breakout to both measure both the high side voltage and DC current draw over I2C with 1% precision. Most current-measuring devices such as our current panel meter are only good for low side measuring. That means that unless you want to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
  ESP32 wrover cam: ESP32-WROVER -> A powerful and small controller with onboard camera and wireless.
